# Fritzing sketch GPIO-Raspi (saved by Fritzing 0.8.7b)
breadboards: 1

parts:
  Raspberry_Pi_B_rev1 = Raspberry Pi B rev2
  LED1 = LED - 3mm [color="White (4500K)" package="3 mm [THT]"]
  J1 = Basic Servo
  Parte1 = SRF05 Ultrasonic Rangefinder
  R1 = Resistor [tolerance=±5% resistance=220 package=THT]
  R2 = Resistor [tolerance=±1% resistance=1k package=THT]

nets:
  5V: Raspberry_Pi_B_rev1.5V, Parte1.VCC
  GND: Raspberry_Pi_B_rev1.GND, LED1.anode, Parte1.GND
  N1: Raspberry_Pi_B_rev1.GPIO_17, J1.pulse
  N2: Raspberry_Pi_B_rev1.GPIO_27, Parte1.Trig
  N3: Raspberry_Pi_B_rev1.GPIO_22, R2.Pin_0
  N4: Raspberry_Pi_B_rev1.GPIO_4, R1.Pin_1
  N5: LED1.cathode, R1.Pin_0
  N6: Parte1.Echo, R2.Pin_1
